# Fritzing sketch Connection (saved by Fritzing 0.9.3b)

parts:
  U1 = NodeMCU V1.0
  Parça1 = Arduino Uno (Rev3) - ICSP
  Parça2 = Triple Axis Accelerometer Breakout - ADXL345
  hc-sr1 = hc-sr04
  J1 = Piezo Speaker

nets:
  N1: U1.D1, Parça2.SCL
  N2: U1.D2, Parça2.SDA
  3V3: U1.3V3, Parça2.VCC
  GND: U1.GND, Parça2.GND, J1.pin1
  N3: U1.D5, hc-sr1.Echo
  N4: U1.D6, hc-sr1.Trig
  N5: U1.D8, J1.pin2
  5V: Parça1.5V, hc-sr1.VCC
  GND_2: Parça1.GND, hc-sr1.GND

custom parts:
  NodeMCU V1.0: ESP8266 based NodeMCU
